# Fritzing sketch pcb-2 (saved by Fritzing 1.0.2b)
circuit board: 11.352cm x 9.26321cm
breadboards: 1

parts:
  Switch = Camdenboss CTB0158-2 [part_number=CTB0158-2 package=THT]
  IC1 = Voltage Regulator [package=to220-igo]
  Right_Motor = Camdenboss CTB0158-3 [part_number=CTB0158-3 package=THT]
  Left_Motor = Camdenboss CTB0158-3 [part_number=CTB0158-3 package=THT]
  ESC_Output = Camdenboss CTB0158-3 [part_number=CTB0158-3 package=THT]
  ESC_Output_2 = Camdenboss CTB0158-3 [part_number=CTB0158-3 package=THT]
  +_ESC_Power_- = Camdenboss CTB0158-2 [part_number=CTB0158-2 package=THT]
  +_ESC_Power_-_2 = Camdenboss CTB0158-2 [part_number=CTB0158-2 package=THT]
  U1 = SWITCH-SPST-2 [package=switch-spst-vertical]
  C1 = Electrolytic Capacitor [capacitance=1µF voltage=50V package="200 mil [THT, electrolytic]"]
  M1 = DOIT Esp32 DevKit v1 (30 pins long, 11 pins width) [part_number=ESP32S-PIN30]
  C2 = Electrolytic Capacitor [capacitance=4.7mF voltage=25V package="200 mil [THT, electrolytic]"]
  +_Battery_- = Camdenboss CTB0158-2 [part_number=CTB0158-2 package=THT]
  ESC_Control = screw terminal, 3 pins
  ESC_Control1 = screw terminal, 3 pins
  GPS = screw terminal, 4 pins
  Magnetometer = screw terminal, 4 pins

nets:
  N1: Switch.pin1, +_Battery_-.pin2
  N2: Switch.pin2, IC1.IN, +_ESC_Power_-.pin2, +_ESC_Power_-_2.pin2, C2.+
  N3: Switch.terminal_1, U1.P
  N4: Switch.terminal_2, U1.O
  GND: IC1.GND, +_ESC_Power_-.pin1, +_ESC_Power_-_2.pin1, C1.-, M1.GND, C2.-, +_Battery_-.pin1, ESC_Control.pin3, ESC_Control1.pin3, GPS.pin4, Magnetometer.pin2
  N5: IC1.OUT, C1.+, M1.VIN
  N6: Right_Motor.pin1, ESC_Output.pin1
  N7: Right_Motor.pin2, ESC_Output.pin2
  N8: Right_Motor.pin3, ESC_Output.pin3
  N9: Left_Motor.pin1, ESC_Output_2.pin1
  N10: Left_Motor.pin2, ESC_Output_2.pin2
  N11: Left_Motor.pin3, ESC_Output_2.pin3
  N12: M1.3V3, GPS.pin1, Magnetometer.pin1
  N13: M1.TX2, ESC_Control.pin1
  N14: M1.D5, ESC_Control1.pin1
  N15: M1.D18, GPS.pin3
  N16: M1.D19, GPS.pin2
  N17: M1.D21, Magnetometer.pin4
  N18: M1.D22, Magnetometer.pin3

custom parts:
  DOIT Esp32 DevKit v1 (30 pins long, 11 pins width): The DOIT Esp32 DevKit v1 is one of the development board created by DOIT to evaluate the ESP-WROOM-32 module. It is based on the ESP32 microcontroller that boasts Wifi, Bluetooth, Ethernet and Low Power support all in a single chip. (vanepp) made breadboard work, adjusted pin numbering and labels and reduced size of schematic and cleaned up pcb. This chip is 30pins long (2 x15) and 11 pins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
